# Fritzing sketch SensorHut (saved by Fritzing 0.9.6b)

parts:
  Charging_moduleArduino_uno = Arduino Uno (Rev3) - ICSP
  ST7789_LCD = Nokia 6100 Color LCD [package=nokia6100_lcd]
  BNP280 = BME280 Breakout
  Photoresistor = PHOTOCELL [package=photocell]
  R2 = Resistor [tolerance=±1% resistance=10k package="0402 [SMD]"]
  RTC = Real Time Clock Module - DS1307 RTC Breakout Board
  DHT11 = Humidity Sensor - HIH-4030 Breakout
  Passive_buzzer = Buzzer 12mm [package=buzzer-12mm-ns]
  Battery = LIPO-2000mAh [package=lipo-2000]
  5V_Solar_cell = SOLAR-IXYS [package=solarbit-12x1]
  Charging_module = MAX1555 Lithium Charger IC [package=sot23-5]
  3_7V_to_5V_DC-DC_converter = V_REG_MIC5235 [package=sot23-5]
  Solar_panel_controller = V_REG_MIC5235 [package=sot23-5]
  Q1 = NPN-Transistor [package="TO92 [THT]"]
  LED = LED - 5mm [color="Green (570nm)" current=0.030A package="5 mm [THT]"]
  S1 = Pushbutton [package="[THT]"]
  S2 = Pushbutton [package="[THT]"]
  USB-C = USB connector [package=THT]
  S4 = Toggle Switch [package=THT]
  R3 = Resistor [tolerance=±1% resistance=1M package="0402 [SMD]"]

nets:
  N1: Charging_moduleArduino_uno.A0, Photoresistor.P$2
  N2: Charging_moduleArduino_uno.A1, RTC.SCL
  N3: Charging_moduleArduino_uno.A2, RTC.SDA
  N4: Charging_moduleArduino_uno.A3, R3.Pin_1
  N5: Charging_moduleArduino_uno.A4/SDA, BNP280.SDI/SDA
  5V: Charging_moduleArduino_uno.5V, ST7789_LCD.VDIGITAL, ST7789_LCD.VDISPLAY, R2.Pin_1, RTC.5V, DHT11.VCC, 3_7V_to_5V_DC-DC_converter.OUT
  GND: Charging_moduleArduino_uno.GND, ST7789_LCD.CS, ST7789_LCD.GND, Passive_buzzer.2, Battery.-, 5V_Solar_cell.C, Charging_module.GND, 3_7V_to_5V_DC-DC_converter.GND, Solar_panel_controller.GND, Q1.E, S1.Pin_3, S1.Pin_4, S2.Pin_3, S2.Pin_4, USB-C.GND, USB-C.chassis5, USB-C.chassis6
  N6: Charging_moduleArduino_uno.D8, LED.cathode
  N7: Charging_moduleArduino_uno.D9_PWM, ST7789_LCD.DIO
  N8: Charging_moduleArduino_uno.D10_PWM/SS, ST7789_LCD.RESET
  N9: Charging_moduleArduino_uno.D11_PWM/MOSI, ST7789_LCD.VLED, LED.anode
  N10: Charging_moduleArduino_uno.D12/MISO, Q1.B
  N11: Charging_moduleArduino_uno.D13/SCK, ST7789_LCD.SCK
  N12: Charging_moduleArduino_uno.A5/SCL, BNP280.SCK/SCL
  N13: Charging_moduleArduino_uno.D2, S1.Pin_2
  N14: Charging_moduleArduino_uno.D3_PWM, S2.Pin_1, S2.Pin_2
  N15: Charging_moduleArduino_uno.D4, RTC.SQW
  N16: Charging_moduleArduino_uno.D5_PWM, Passive_buzzer.1
  N17: Charging_moduleArduino_uno.D6_PWM, ST7789_LCD.LEDGND
  N18: Charging_moduleArduino_uno.D7, DHT11.OUT
  Colector: BNP280.GND, Photoresistor.P$1, R2.Pin_0, RTC.GND, DHT11.GND, Q1.C
  3.3V: BNP280.3.3V
  N19: Battery.+, Charging_module.BATT, 3_7V_to_5V_DC-DC_converter.IN, Solar_panel_controller.OUT, S4.COM, R3.Pin_0
  N20: 5V_Solar_cell.A, Solar_panel_controller.IN, Solar_panel_controller.EN
  N21: Charging_module.USB, USB-C.5V
  N22: 3_7V_to_5V_DC-DC_converter.EN, S4.L2

notes:
  Power module
  Sesor Hut
